// Logisim project 16-Bit Adder.circ as structural Verilog: 1 circuit, main circuit main
module main (
  output [15:0] out_1
);

  wire and_1_out, full_adder_1_c_out, full_adder_2_c_out, full_adder_3_c_out, full_adder_4_c_out,
       full_adder_5_c_out, full_adder_6_c_out, full_adder_7_c_out, full_adder_8_c_out, full_adder_9_c_out,
       full_adder_10_c_out, full_adder_11_c_out, full_adder_12_c_out, full_adder_13_c_out,
       full_adder_14_c_out, full_adder_15_c_out, undriven, undriven_2;

  xor xor_1 (out_1[0], undriven_2, undriven);
  and and_1 (and_1_out, undriven, undriven_2);
  Full_Adder full_adder_1 (.Sum(out_1[4]), .C_in(full_adder_12_c_out), .C_out(full_adder_1_c_out));  // open: A, B
  Full_Adder full_adder_2 (.Sum(out_1[8]), .C_in(full_adder_13_c_out), .C_out(full_adder_2_c_out));  // open: A, B
  Full_Adder full_adder_3 (.Sum(out_1[12]), .C_in(full_adder_14_c_out), .C_out(full_adder_3_c_out));  // open: A, B
  Full_Adder full_adder_4 (.Sum(out_1[1]), .C_in(and_1_out), .C_out(full_adder_4_c_out));  // open: A, B
  Full_Adder full_adder_5 (.Sum(out_1[5]), .C_in(full_adder_1_c_out), .C_out(full_adder_5_c_out));  // open: A, B
  Full_Adder full_adder_6 (.Sum(out_1[9]), .C_in(full_adder_2_c_out), .C_out(full_adder_6_c_out));  // open: A, B
  Full_Adder full_adder_7 (.Sum(out_1[13]), .C_in(full_adder_3_c_out), .C_out(full_adder_7_c_out));  // open: A, B
  Full_Adder full_adder_8 (.Sum(out_1[2]), .C_in(full_adder_4_c_out), .C_out(full_adder_8_c_out));  // open: A, B
  Full_Adder full_adder_9 (.Sum(out_1[6]), .C_in(full_adder_5_c_out), .C_out(full_adder_9_c_out));  // open: A, B
  Full_Adder full_adder_10 (.Sum(out_1[10]), .C_in(full_adder_6_c_out), .C_out(full_adder_10_c_out));  // open: A, B
  Full_Adder full_adder_11 (.Sum(out_1[14]), .C_in(full_adder_7_c_out), .C_out(full_adder_11_c_out));  // open: A, B
  Full_Adder full_adder_12 (.Sum(out_1[3]), .C_in(full_adder_8_c_out), .C_out(full_adder_12_c_out));  // open: A, B
  Full_Adder full_adder_13 (.Sum(out_1[7]), .C_in(full_adder_9_c_out), .C_out(full_adder_13_c_out));  // open: A, B
  Full_Adder full_adder_14 (.Sum(out_1[11]), .C_in(full_adder_10_c_out), .C_out(full_adder_14_c_out));  // open: A, B
  Full_Adder full_adder_15 (.Sum(out_1[15]), .C_in(full_adder_11_c_out), .C_out(full_adder_15_c_out));  // open: A, B
endmodule
