// Logisim project COMP_303_FinalProject.circ as structural Verilog: 6 circuits, main circuit Register File
module Register_File (
  input  [15:0] WriteData,
  input  RegWrite,
  input  [3:0] ReadAddr1,
  input  [3:0] WriteAddr,
  input  in_5,
  input  [3:0] ReadAddr2,
  output [15:0] ReadData1,
  output [15:0] ReadData2
);

  wire decoder_1_out0, decoder_1_out1, decoder_1_out2, decoder_1_out3, decoder_1_out4, decoder_1_out5,
       decoder_1_out6, decoder_1_out7, decoder_1_out8, decoder_1_out9, decoder_1_out10, decoder_1_out11,
       decoder_1_out12, decoder_1_out13, decoder_1_out14, decoder_1_out15;
  wire [15:0] reg0_q, reg1_q, reg2_q, reg3_q, register_1_q, register_2_q, register_3_q, register_4_q,
       register_5_q, register_6_q, register_7_q, register_8_q, register_9_q, register_10_q, register_11_q,
       register_12_q;

  Decoder #(.select(4)) decoder_1 (
    .out0(decoder_1_out0), .out1(decoder_1_out1), .out2(decoder_1_out2), .out3(decoder_1_out3),
    .out4(decoder_1_out4), .out5(decoder_1_out5), .out6(decoder_1_out6), .out7(decoder_1_out7),
    .out8(decoder_1_out8), .out9(decoder_1_out9), .out10(decoder_1_out10), .out11(decoder_1_out11),
    .out12(decoder_1_out12), .out13(decoder_1_out13), .out14(decoder_1_out14), .out15(decoder_1_out15),
    .sel(WriteAddr), .en(RegWrite));
  Register #(.width(16)) reg0 (.D(WriteData), .en(decoder_1_out0), .Q(reg0_q), .clk(in_5));  // open: clr
  Register #(.width(16)) register_1 (.D(WriteData), .en(decoder_1_out4), .Q(register_1_q), .clk(in_5));  // open: clr
  Register #(.width(16)) register_2 (.D(WriteData), .en(decoder_1_out8), .Q(register_2_q), .clk(in_5));  // open: clr
  Register #(.width(16)) register_3 (.D(WriteData), .en(decoder_1_out12), .Q(register_3_q), .clk(in_5));  // open: clr
  Register #(.width(16)) reg1 (.D(WriteData), .en(decoder_1_out1), .Q(reg1_q), .clk(in_5));  // open: clr
  Register #(.width(16)) register_4 (.D(WriteData), .en(decoder_1_out5), .Q(register_4_q), .clk(in_5));  // open: clr
  Register #(.width(16)) register_5 (.D(WriteData), .en(decoder_1_out9), .Q(register_5_q), .clk(in_5));  // open: clr
  Register #(.width(16)) register_6 (.D(WriteData), .en(decoder_1_out13), .Q(register_6_q), .clk(in_5));  // open: clr
  Register #(.width(16)) reg2 (.D(WriteData), .en(decoder_1_out2), .Q(reg2_q), .clk(in_5));  // open: clr
  Register #(.width(16)) register_7 (.D(WriteData), .en(decoder_1_out6), .Q(register_7_q), .clk(in_5));  // open: clr
  Register #(.width(16)) register_8 (.D(WriteData), .en(decoder_1_out10), .Q(register_8_q), .clk(in_5));  // open: clr
  Register #(.width(16)) register_9 (.D(WriteData), .en(decoder_1_out14), .Q(register_9_q), .clk(in_5));  // open: clr
  Register #(.width(16)) reg3 (.D(WriteData), .en(decoder_1_out3), .Q(reg3_q), .clk(in_5));  // open: clr
  Register #(.width(16)) register_10 (.D(WriteData), .en(decoder_1_out7), .Q(register_10_q), .clk(in_5));  // open: clr
  Register #(.width(16)) register_11 (.D(WriteData), .en(decoder_1_out11), .Q(register_11_q), .clk(in_5));  // open: clr
  Register #(.width(16)) register_12 (.D(WriteData), .en(decoder_1_out15), .Q(register_12_q), .clk(in_5));  // open: clr
  Multiplexer #(.select(4), .width(16)) multiplexer_1 (
    .in0(reg0_q), .in1(reg1_q), .in2(reg2_q), .in3(reg3_q), .in4(register_1_q), .in5(register_4_q),
    .in6(register_7_q), .in7(register_10_q), .in8(register_2_q), .in9(register_5_q), .in10(register_8_q),
    .in11(register_11_q), .in12(register_3_q), .in13(register_6_q), .in14(register_9_q),
    .in15(register_12_q), .out(ReadData1), .sel(ReadAddr1));  // open: en
  Multiplexer #(.select(4), .width(16)) multiplexer_2 (
    .in0(reg0_q), .in1(reg1_q), .in2(reg2_q), .in3(reg3_q), .in4(register_1_q), .in5(register_4_q),
    .in6(register_7_q), .in7(register_10_q), .in8(register_2_q), .in9(register_5_q), .in10(register_8_q),
    .in11(register_11_q), .in12(register_3_q), .in13(register_6_q), .in14(register_9_q),
    .in15(register_12_q), .out(ReadData2), .sel(ReadAddr2));  // open: en
endmodule

module Full_Adder (
  input  A,
  input  B,
  input  C_in,
  output Sum,
  output C_out
);

  wire and_1_out, and_2_out, xor_1_out;

  xor xor_1 (xor_1_out, A, B);
  and and_1 (and_1_out, C_in, xor_1_out);
  and and_2 (and_2_out, A, B);
  xor xor_2 (Sum, xor_1_out, C_in);
  or or_1 (C_out, and_1_out, and_2_out);
endmodule

module _16_Bit_Adder (
  input  [15:0] in_1,
  input  [15:0] in_2,
  output [15:0] out_3,
  output out_4
);

  wire and_1_out, full_adder_1_c_out, full_adder_2_c_out, full_adder_3_c_out, full_adder_4_c_out,
       full_adder_5_c_out, full_adder_6_c_out, full_adder_7_c_out, full_adder_8_c_out, full_adder_9_c_out,
       full_adder_10_c_out, full_adder_11_c_out, full_adder_12_c_out, full_adder_13_c_out,
       full_adder_14_c_out;

  and and_1 (and_1_out, in_2[0], in_1[0]);
  Full_Adder full_adder_1 (
    .A(in_1[4]), .B(in_2[4]), .C_in(full_adder_12_c_out), .Sum(out_3[4]), .C_out(full_adder_1_c_out));
  Full_Adder full_adder_2 (
    .A(in_1[8]), .B(in_2[8]), .C_in(full_adder_13_c_out), .Sum(out_3[8]), .C_out(full_adder_2_c_out));
  Full_Adder full_adder_3 (
    .A(in_1[12]), .B(in_2[12]), .C_in(full_adder_14_c_out), .Sum(out_3[12]), .C_out(full_adder_3_c_out));
  xor xor_1 (out_3[0], in_1[0], in_2[0]);
  Full_Adder full_adder_4 (.A(in_1[1]), .B(in_2[1]), .C_in(and_1_out), .Sum(out_3[1]), .C_out(full_adder_4_c_out));
  Full_Adder full_adder_5 (
    .A(in_1[5]), .B(in_2[5]), .C_in(full_adder_1_c_out), .Sum(out_3[5]), .C_out(full_adder_5_c_out));
  Full_Adder full_adder_6 (
    .A(in_1[9]), .B(in_2[9]), .C_in(full_adder_2_c_out), .Sum(out_3[9]), .C_out(full_adder_6_c_out));
  Full_Adder full_adder_7 (
    .A(in_1[13]), .B(in_2[13]), .C_in(full_adder_3_c_out), .Sum(out_3[13]), .C_out(full_adder_7_c_out));
  Full_Adder full_adder_8 (
    .A(in_1[2]), .B(in_2[2]), .C_in(full_adder_4_c_out), .Sum(out_3[2]), .C_out(full_adder_8_c_out));
  Full_Adder full_adder_9 (
    .A(in_1[6]), .B(in_2[6]), .C_in(full_adder_5_c_out), .Sum(out_3[6]), .C_out(full_adder_9_c_out));
  Full_Adder full_adder_10 (
    .A(in_1[10]), .B(in_2[10]), .C_in(full_adder_6_c_out), .Sum(out_3[10]), .C_out(full_adder_10_c_out));
  Full_Adder full_adder_11 (
    .A(in_1[14]), .B(in_2[14]), .C_in(full_adder_7_c_out), .Sum(out_3[14]), .C_out(full_adder_11_c_out));
  Full_Adder full_adder_12 (
    .A(in_1[3]), .B(in_2[3]), .C_in(full_adder_8_c_out), .Sum(out_3[3]), .C_out(full_adder_12_c_out));
  Full_Adder full_adder_13 (
    .A(in_1[7]), .B(in_2[7]), .C_in(full_adder_9_c_out), .Sum(out_3[7]), .C_out(full_adder_13_c_out));
  Full_Adder full_adder_14 (
    .A(in_1[11]), .B(in_2[11]), .C_in(full_adder_10_c_out), .Sum(out_3[11]), .C_out(full_adder_14_c_out));
  Full_Adder full_adder_15 (.A(in_1[15]), .B(in_2[15]), .C_in(full_adder_11_c_out), .Sum(out_3[15]), .C_out(out_4));
endmodule

module ALU (
  input  [15:0] in_1,
  input  [15:0] in_2,
  input  [5:0] ALUOp,
  input  CLK,
  output zero,
  output [15:0] out_6
);

  wire comparator_1_eq, comparator_2_gt, comparator_3_eq, comparator_4_eq, comparator_5_lt, not_1_out,
       or_1_out;
  wire [15:0] and_1_out, bit_extender_1_out, Hi_q, Lo_q, multiplexer_1_out, multiplier_1_cout,
       multiplier_1_out, n16_bit_adder_1_out_3, or_2_out, shifter_1_out, subtractor_1_out;

  Comparator #(.width(16)) comparator_1 (.a(in_1), .b(in_2), .eq(comparator_1_eq));  // open: gt, lt
  Comparator #(.width(16)) comparator_2 (.a(in_1), .b({16{1'b0}}), .gt(comparator_2_gt));  // open: eq, lt
  not not_1 (not_1_out, comparator_2_gt);
  Multiplexer #(.width(16), .enable("false")) multiplexer_1 (
    .in0(in_1), .in1(in_2), .out(multiplexer_1_out), .sel(comparator_3_eq));
  Multiplexer #(.select(2), .enable("false")) multiplexer_2 (
    .in0(1'b0), .in1(comparator_1_eq), .in2(not_1_out), .in3(1'b0), .out(zero), .sel(ALUOp[5:4]));
  Comparator #(.width(4)) comparator_3 (.a(4'b0011), .b(ALUOp[3:0]), .eq(comparator_3_eq));  // open: gt, lt
  Comparator #(.width(4)) comparator_4 (.a(ALUOp[3:0]), .b(4'b1111), .eq(comparator_4_eq));  // open: gt, lt
  or or_1 (or_1_out, comparator_3_eq, comparator_4_eq);
  _16_Bit_Adder u_16_bit_adder_1 (.in_1(in_1), .in_2(in_2), .out_3(n16_bit_adder_1_out_3));  // open: out_4
  Subtractor #(.width(16)) subtractor_1 (.a(in_1), .b(in_2), .out(subtractor_1_out));  // open: bin, bout
  Multiplier #(.width(16)) multiplier_1 (
    .a(in_1), .b(multiplexer_1_out), .out(multiplier_1_out), .cout(multiplier_1_cout));  // open: cin
  assign and_1_out = in_1 & in_2;  // AND_Gate and_1, 16 bits wide
  assign or_2_out = in_1 | in_2;  // OR_Gate or_2, 16 bits wide
  Shifter #(.width(16)) shifter_1 (.in(in_1), .\dist (in_2[9:6]), .out(shifter_1_out));
  Comparator #(.width(16)) comparator_5 (.a(in_1), .b(in_2), .lt(comparator_5_lt));  // open: gt, eq
  Register #(.width(16)) Hi (.D(multiplier_1_cout), .en(or_1_out), .Q(Hi_q), .clk(CLK));  // open: clr
  Register #(.width(16)) Lo (.D(multiplier_1_out), .en(or_1_out), .Q(Lo_q), .clk(CLK));  // open: clr
  assign bit_extender_1_out = {{15{1'b0}}, comparator_5_lt};  // Bit_Extender bit_extender_1
  Multiplexer #(.select(4), .width(16), .enable("false")) multiplexer_3 (
    .in0(n16_bit_adder_1_out_3), .in1(subtractor_1_out), .in3(and_1_out), .in4(or_2_out),
    .in5(n16_bit_adder_1_out_3), .in6(shifter_1_out), .in7(bit_extender_1_out), .in8(Hi_q), .in9(Lo_q),
    .out(out_6), .sel(ALUOp[3:0]));  // open: in2, in10, in11, in12, in13, in14, in15

  // Notes on the sheet:
  //   01: beq, 10: blez
endmodule

module CPU (
);

  wire alu_1_zero, and_1_out, clock_1_out, control_unit_1_alusrc, control_unit_1_branch,
       control_unit_1_memread, control_unit_1_memtoreg, control_unit_1_memwrite, control_unit_1_pcsrc,
       control_unit_1_regdst, control_unit_1_regwrite;
  wire [3:0] multiplexer_1_out;
  wire [5:0] control_unit_1_aluop;
  wire [15:0] alu_1_out_6, multiplexer_2_out, multiplexer_3_out, multiplexer_4_out, multiplexer_5_out,
       n16_bit_adder_1_out_3, n16_bit_adder_2_out_3, PC_q, ram_1_data, register_file_1_readdata1,
       register_file_1_readdata2;
  wire [31:0] rom_1_data;

  Register #(.width(16)) PC (.D(multiplexer_3_out), .en(1'b1), .Q(PC_q), .clk(clock_1_out));  // open: clr
  _16_Bit_Adder u_16_bit_adder_1 (.in_1(PC_q), .in_2(16'h1), .out_3(n16_bit_adder_1_out_3));  // open: out_4
  ROM #(.addrWidth(16), .dataWidth(32)) rom_1 (.addr(PC_q), .data(rom_1_data));  // open: sel
  Control_Unit control_unit_1 (
    .in_1(rom_1_data[31:26]), .ALUOp(control_unit_1_aluop), .RegWrite(control_unit_1_regwrite),
    .ALUSrc(control_unit_1_alusrc), .MemWrite(control_unit_1_memwrite), .MemRead(control_unit_1_memread),
    .MemToReg(control_unit_1_memtoreg), .Branch(control_unit_1_branch), .RegDst(control_unit_1_regdst),
    .PCSrc(control_unit_1_pcsrc));
  Multiplexer #(.width(4), .enable("false")) multiplexer_1 (
    .in0(rom_1_data[19:16]), .in1(rom_1_data[14:11]), .out(multiplexer_1_out), .sel(control_unit_1_regdst));
  Register_File register_file_1 (
    .WriteData(multiplexer_5_out), .RegWrite(control_unit_1_regwrite), .ReadData1(register_file_1_readdata1),
    .ReadAddr1(rom_1_data[24:21]), .ReadData2(register_file_1_readdata2), .ReadAddr2(rom_1_data[19:16]),
    .WriteAddr(multiplexer_1_out), .in_5(clock_1_out));
  Clock clock_1 (.out(clock_1_out));
  _16_Bit_Adder u_16_bit_adder_2 (
    .in_1(n16_bit_adder_1_out_3), .in_2(rom_1_data[15:0]), .out_3(n16_bit_adder_2_out_3));  // open: out_4
  ALU alu_1 (
    .in_1(register_file_1_readdata1), .in_2(multiplexer_2_out), .out_6(alu_1_out_6), .CLK(clock_1_out),
    .ALUOp(control_unit_1_aluop), .zero(alu_1_zero));
  Multiplexer #(.width(16), .enable("false")) multiplexer_2 (
    .in0(register_file_1_readdata2), .in1(rom_1_data[15:0]), .out(multiplexer_2_out),
    .sel(control_unit_1_alusrc));
  and and_1 (and_1_out, control_unit_1_branch, alu_1_zero);
  Multiplexer #(.width(16), .enable("false")) multiplexer_3 (
    .in0(multiplexer_4_out), .in1(rom_1_data[15:0]), .out(multiplexer_3_out), .sel(control_unit_1_pcsrc));
  Multiplexer #(.width(16), .enable("false")) multiplexer_4 (
    .in0(n16_bit_adder_1_out_3), .in1(n16_bit_adder_2_out_3), .out(multiplexer_4_out), .sel(and_1_out));
  RAM #(.addrWidth(16), .dataWidth(16), .bus("separate")) ram_1 (
    .addr(alu_1_out_6), .din(register_file_1_readdata2), .data(ram_1_data), .str(control_unit_1_memwrite),
    .clk(clock_1_out), .ld(control_unit_1_memread));  // open: sel, clr
  Multiplexer #(.width(16), .enable("false")) multiplexer_5 (
    .in0(alu_1_out_6), .in1(ram_1_data), .out(multiplexer_5_out), .sel(control_unit_1_memtoreg));

  // Notes on the sheet:
  //   opcode
  //   rs
  //   rt
  //   rd
  //   shamt
  //   funct
  //   contents of rom_1 (hex, n*v repeats v):
  //   14080000 14090004 140a0008 14010004 14050002 14020000 3022000b 481800 28630000 492000 28840000
  //   641800 8602800 24001800 4a1800 2c660000 14420001 38000006
  //   address
  //   ALUSrc
endmodule

module Control_Unit (
  input  [5:0] in_1,
  output [5:0] ALUOp,
  output Branch,
  output RegDst,
  output MemRead,
  output MemToReg,
  output MemWrite,
  output ALUSrc,
  output RegWrite,
  output PCSrc
);

  wire and_2_out, comparator_3_gt, comparator_4_lt, comparator_5_gt, comparator_6_eq, comparator_7_eq,
       comparator_8_eq, comparator_9_lt, comparator_10_eq, comparator_14_eq, not_1_out, not_2_out, not_3_out;

  Comparator #(.width(6), .mode("unsigned")) comparator_1 (.a(in_1), .b(6'b001101), .eq(ALUOp[5]));  // open: gt, lt
  Comparator #(.width(6), .mode("unsigned")) comparator_2 (.a(in_1), .b(6'b001100), .eq(ALUOp[4]));  // open: gt, lt
  Comparator #(.width(6), .mode("unsigned")) comparator_3 (
    .a(in_1), .b(6'b001011), .gt(comparator_3_gt));  // open: eq, lt
  Comparator #(.width(6), .mode("unsigned")) comparator_4 (
    .a(in_1), .b(6'b001111), .lt(comparator_4_lt));  // open: gt, eq
  Comparator #(.width(6), .mode("unsigned")) comparator_5 (
    .a(in_1), .b(6'b001010), .gt(comparator_5_gt));  // open: eq, lt
  Comparator #(.width(6), .mode("unsigned")) comparator_6 (
    .a(in_1), .b(6'b001100), .eq(comparator_6_eq));  // open: gt, lt
  not not_1 (not_1_out, comparator_6_eq);
  Comparator #(.width(6), .mode("unsigned")) comparator_7 (
    .a(in_1), .b(6'b000101), .eq(comparator_7_eq));  // open: gt, lt
  Comparator #(.width(6), .mode("unsigned")) comparator_8 (
    .a(in_1), .b(6'b000110), .eq(comparator_8_eq));  // open: gt, lt
  Comparator #(.width(6), .mode("unsigned")) comparator_9 (
    .a(in_1), .b(6'b001011), .lt(comparator_9_lt));  // open: gt, eq
  not not_2 (not_2_out, comparator_10_eq);
  Comparator #(.width(6), .mode("unsigned")) comparator_10 (
    .a(in_1), .b(6'b000010), .eq(comparator_10_eq));  // open: gt, lt
  Comparator #(.width(6), .mode("unsigned")) comparator_11 (.a(in_1), .b(6'b001110), .eq(PCSrc));  // open: gt, lt
  and and_1 (Branch, comparator_3_gt, comparator_4_lt);
  and and_2 (and_2_out, comparator_5_gt, not_1_out);
  and and_3 (RegWrite, comparator_9_lt, not_2_out);
  Comparator #(.width(6), .mode("unsigned")) comparator_12 (.a(in_1), .b(6'b001010), .eq(MemRead));  // open: gt, lt
  Comparator #(.width(6), .mode("unsigned")) comparator_13 (.a(in_1), .b(6'b001011), .eq(MemWrite));  // open: gt, lt
  or or_1 (ALUSrc, and_2_out, comparator_7_eq, comparator_8_eq);
  not not_3 (not_3_out, MemRead);
  Comparator #(.width(6), .mode("unsigned")) comparator_14 (
    .a(in_1), .b(6'b000101), .eq(comparator_14_eq));  // open: gt, lt
  nand nand_1 (RegDst, comparator_14_eq, not_3_out);

  assign ALUOp[3:0] = in_1[3:0];
  assign MemToReg = MemRead;
endmodule
