// Logisim project FullAdder.circ as structural Verilog: 1 circuit, main circuit Full Adder
module Full_Adder (
  input  A,
  input  B,
  input  C_in,
  output Sum,
  output C_out
);

  wire and_1_out, and_2_out, or_1_out, xor_1_out, xor_2_out;

  xor xor_1 (xor_1_out, A, B);
  xor xor_2 (xor_2_out, xor_1_out, C_in);
  and and_1 (and_1_out, C_in, xor_1_out);
  and and_2 (and_2_out, A, B);
  or or_1 (or_1_out, and_1_out, and_2_out);
endmodule
